# Fritzing sketch L293D_first_test_2 (saved by Fritzing 0.9.3b)
breadboards: 1

parts:
  Part1 = Arduino Uno (Rev3)
  Left = Vibration Motor- ROB-08449 [package=vibe-motor-10mm]
  C1 = Capacitor [part_number="0.1 uF" package=cap-pth-small2]
  IC1 = L293D [package=THT]
  C2 = Capacitor [part_number="0.1 uF" package=cap-pth-small2]
  Right = Vibration Motor- ROB-08449 [package=vibe-motor-10mm]
  BAT1 = BC9VPC [package=bc9vpc]
  Part2 = Thumb Joystick
  S1 = SPST Switch [package=switch-spdt-smd]
  Part3 = Bluetooth HC-05 Macho

nets:
  N1: Part1.A0, Part2.HORZ
  N2: Part1.A1, Part2.VERT
  N3: Part1.D8, Part3.RXD
  N4: Part1.D9_PWM, Part3.TXD
  N5: Part1.D10_PWM/SS, IC1.In_3
  N6: Part1.D11_PWM/MOSI, IC1.In_4
  N7: Part1.D2, IC1.Enable_1
  N8: Part1.D3_PWM, IC1.Enable_2
  N9: Part1.D5_PWM, IC1.In_1
  N10: Part1.D6_PWM, IC1.In_2
  VCC: Part1.5V, IC1.+V, Part2.VCC, Part3.VCC
  GND: Part1.GND, IC1.0V, BAT1.V-, Part2.GND, Part3.GND
  N11: Part1.VIN, IC1.+Vmotor, S1.P
  N12: Left.+, C1.1, IC1.Out_2_(_Controlled_by_Enable_1_)
  N13: Left.-, C1.2, IC1.Out_1_(_Controlled_by_Enable_1_)
  N14: IC1.Out_3_(_Controlled_by_Enable_2_), C2.1, Right.+
  N15: IC1.Out_4_(_Controlled_by_Enable_2_), C2.2, Right.-
  N16: BAT1.V+, S1.S
