# Fritzing sketch L298N_final (saved by Fritzing 0.9.3b)
breadboards: 1

parts:
  Part1 = Arduino Uno (Rev3)
  C1 = Capacitor [part_number="0.1 uF" package=cap-pth-small2]
  C2 = Capacitor [part_number="0.1 uF" package=cap-pth-small2]
  Part3 = Bluetooth HC-05 Macho
  Part4 = Motor Driver 1A Dual TB6612FNG
  J1 = Basic Servo
  VCC2 = Battery
  M1 = DC Motor
  M2 = DC Motor
  VCC4 = Battery
  VCC1 = Battery
  BAT1 = BC9VPC [package=bc9vpc]
  Part5 = SHT1x-Breakout
  LED1 = LED - 3mm [color="Red (633nm)" package="3 mm [THT]"]

nets:
  N1: Part1.A4/SDA, Part5.DATA
  N2: Part1.A5/SCL, Part5.SCK
  N3: Part1.D8, Part3.RXD
  N4: Part1.D9_PWM, Part3.TXD
  N5: Part1.D10_PWM/SS, Part4.BIN1
  N6: Part1.D11_PWM/MOSI, Part4.BIN2
  N7: Part1.D12/MISO, J1.pulse
  GND: Part1.GND, Part3.GND, Part4.GND, BAT1.V-, Part5.GND, LED1.cathode
  N8: Part1.D2, LED1.anode
  N9: Part1.D3_PWM, Part4.PWMA
  N10: Part1.D5_PWM, Part4.PWMB
  N11: Part1.D6_PWM, Part4.AIN1
  N12: Part1.D7, Part4.AIN2
  3V3: Part1.3V3, Part5.VCC
  5V: Part1.5V, Part3.VCC
  N13: Part1.VIN, Part4.VM, VCC2.+
  N14: C1.1, Part4.B01, M1.pin_1
  N15: C1.2, Part4.B02, M1.pin_2
  N16: C2.1, Part4.A01, M2.pin_1
  N17: C2.2, Part4.A02, M2.pin_2
  N18: J1.gnd, VCC4.-
  N19: J1.vcc, VCC4.+
  N20: VCC2.-, VCC1.+
  N21: VCC1.-, BAT1.V+
