# Fritzing sketch L298N_v1.0 (saved by Fritzing 0.9.3b)
breadboards: 1

parts:
  Part1 = Arduino Uno (Rev3)
  Left = Vibration Motor- ROB-08449 [package=vibe-motor-10mm]
  C1 = Capacitor [part_number="0.1 uF" package=cap-pth-small2]
  C2 = Capacitor [part_number="0.1 uF" package=cap-pth-small2]
  Right = Vibration Motor- ROB-08449 [package=vibe-motor-10mm]
  BAT1 = BC9VPC [package=bc9vpc]
  Part2 = Thumb Joystick
  Part3 = Bluetooth HC-05 Macho
  Part4 = Motor Driver 1A Dual TB6612FNG  # not connected

nets:
  N1: Part1.A0, Part2.HORZ
  N2: Part1.A1, Part2.VERT
  N3: Part1.D8, Part3.RXD
  N4: Part1.D9_PWM, Part3.TXD
  VCC: Part1.5V, Part2.VCC, Part3.VCC
  GND: Part1.GND, BAT1.V-, Part2.GND, Part3.GND
  N5: Part1.VIN, BAT1.V+
  N6: Left.+, C1.1
  N7: Left.-, C1.2
  N8: C2.1, Right.+
  N9: C2.2, Right.-
