# Fritzing sketch L293D_first_test_2 (saved by Fritzing 0.9.3b)
breadboards: 1

parts:
  Part1 = Arduino Uno (Rev3)
  Right = Vibration Motor- ROB-08449 [package=vibe-motor-10mm]
  C1 = Capacitor [part_number="0.1 uF" package=cap-pth-small2]
  IC1 = L293D [package=THT]
  C2 = Capacitor [part_number="0.1 uF" package=cap-pth-small2]
  Left = Vibration Motor- ROB-08449 [package=vibe-motor-10mm]
  BAT1 = BC9VPC [package=bc9vpc]
  Part2 = Thumb Joystick
  S1 = SPST Switch [package=switch-spdt-smd]  # not connected

nets (from the schematic view):
  N1: Part1.A0, Part2.HORZ
  N2: Part1.A1, Part2.VERT
  N3: Part1.D10_PWM/SS, IC1.In_3
  N4: Part1.D11_PWM/MOSI, IC1.In_4
  N5: Part1.D2, IC1.Enable_1
  N6: Part1.D3_PWM, IC1.Enable_2
  N7: Part1.D5_PWM, IC1.In_1
  N8: Part1.D6_PWM, IC1.In_2
  5V: Part1.5V, IC1.+V, Part2.VCC
  GND: Part1.GND, IC1.0V, BAT1.V-, Part2.GND
  N9: Part1.VIN, IC1.+Vmotor, BAT1.V+
  N10: Right.+, C1.1, IC1.Out_2_(_Controlled_by_Enable_1_)
  N11: Right.-, C1.2, IC1.Out_1_(_Controlled_by_Enable_1_)
  N12: IC1.Out_3_(_Controlled_by_Enable_2_), C2.1, Left.+
  N13: IC1.Out_4_(_Controlled_by_Enable_2_), C2.2, Left.-
